// Logisim project PLCPU_MIPS.circ as structural Verilog: 17 circuits, main circuit SCCPU
module SCCPU (
);

  wire alu_2_1_equal, alu_2_1_signed_overflow, and_1_out, and_2_out, clock_1_out, ctrdreg_1_aluscre,
       ctrdreg_1_branche, ctrdreg_1_memtorege, ctrdreg_1_memwritee, ctrdreg_1_regdste, ctrdreg_1_regwritee,
       ctrereg_1_clk1, ctrereg_1_memtoregm, ctrereg_1_memwritem, ctrereg_1_regwritem, ctrwreg_1_clk1,
       ctrwreg_1_memtoregw, ctrwreg_1_regwritew, e_m_reg_1_r1, e_m_reg_1_we1, flush_control_1_d,
       flush_control_1_e, flush_control_1_out_8, hazard_detector_1_is_hazard, hazard_detector_2_is_hazard,
       hazard_detector_3_is_hazard, hazard_detector_4_is_hazard, hazard_detector_5_is_hazard,
       hazard_detector_6_is_hazard, m_w_reg_1_r1, m_w_reg_1_we1, not_1_out, not_2_out, op_decode_1_alu_src,
       op_decode_1_branch, op_decode_1_jump, op_decode_1_mem_2reg, op_decode_1_mem_write, op_decode_1_out_9,
       op_decode_1_out_11, op_decode_1_out_13, op_decode_1_out_15, op_decode_1_out_17, op_decode_1_out_19,
       op_decode_1_reg_dst, op_decode_1_reg_write, or_1_out, RESET_out;
  wire [1:0] multiplexer_7_out, multiplexer_8_out, multiplexer_9_out, multiplexer_10_out, op_decode_1_alu_op;
  wire [4:0] alu_decode_1_alu_ctrl, ctrdreg_1_alucontrole, d_e_reg_1_e_rd, d_e_reg_1_e_rs, d_e_reg_1_e_rt,
       e_m_reg_1_m_write_reg, m_w_reg_1_w_write_reg, multiplexer_3_out;
  wire [7:0] ram_1_p12, ram_1_p13, ram_1_p14, ram_1_p15, rom_1_p2, rom_1_p3, rom_1_p4, rom_1_p5;
  wire [27:0] adder_1_out;
  wire [31:0] adder_2_out, alu_2_1_result, bit_extender_1_out, d_e_reg_1_e_pc4, d_e_reg_1_e_rd1,
       d_e_reg_1_e_rd2, d_e_reg_1_e_sign_imm, e_m_reg_1_m_alu_out, e_m_reg_1_m_write_data, f_d_reg_1_d_inst,
       f_d_reg_1_d_pcplus4, m_w_reg_1_w_alu_out, m_w_reg_1_w_rd, multiplexer_1_out, multiplexer_2_out,
       multiplexer_4_out, multiplexer_5_out, multiplexer_6_out, multiplexer_11_out, regfile_1_rd1,
       regfile_1_rd2, register_1_q, shifter_1_out;
  wire [31:28] adder_1_out_2;

  Multiplexer #(.width(32)) multiplexer_1 (
    .in0({adder_1_out_2, adder_1_out}), .in1(d_e_reg_1_e_pc4), .out(multiplexer_1_out), .sel(and_1_out));
  Multiplexer #(.width(32)) multiplexer_2 (
    .in0(multiplexer_1_out), .in1({adder_1_out_2, f_d_reg_1_d_inst[25:0], 2'b00}), .out(multiplexer_2_out),
    .sel(op_decode_1_jump));
  Register #(.width(32)) register_1 (
    .D(multiplexer_2_out), .en(not_1_out), .clk(clock_1_out), .Q(register_1_q), .clr(RESET_out));
  not not_1 (not_1_out, or_1_out);
  // ROM #(.addrWidth(24), .line("quad")) rom_1: pin names not known; wires that end beside it: register_1_q[23:0], rom_1_p2, rom_1_p3, rom_1_p4, rom_1_p5
  Adder #(.width(32)) adder_1 (.a(register_1_q), .b(32'h4), .out({adder_1_out_2, adder_1_out}));  // open: cin, cout
  Clock clock_1 (.out(clock_1_out));
  Button RESET (.out(RESET_out));
  not not_2 (not_2_out, or_1_out);
  F_D_REG f_d_reg_1 (
    .Inst({rom_1_p2, rom_1_p3, rom_1_p4, rom_1_p5}), .PCplus4({adder_1_out_2, adder_1_out}),
    .R(flush_control_1_d), .WE(not_2_out), .CLK(clock_1_out), .D_Inst(f_d_reg_1_d_inst),
    .D_PCplus4(f_d_reg_1_d_pcplus4));
  FLUSH_CONTROL flush_control_1 (
    .R(RESET_out), .J(op_decode_1_jump), .B(and_1_out), .CLK(clock_1_out), .STALL(or_1_out),
    .D(flush_control_1_d), .E(flush_control_1_e), .out_8(flush_control_1_out_8));
  assign bit_extender_1_out = {{16{f_d_reg_1_d_inst[15]}}, f_d_reg_1_d_inst[15:0]};  // Bit_Extender bit_extender_1
  HAZARD_DETECTOR hazard_detector_1 (
    .REG_DEST(d_e_reg_1_e_rt), .REG_SRC(f_d_reg_1_d_inst[25:21]), .REG_WRITE(ctrdreg_1_memtorege),
    .IS_HAZARD(hazard_detector_1_is_hazard));
  or or_1 (or_1_out, hazard_detector_1_is_hazard, hazard_detector_2_is_hazard);
  HAZARD_DETECTOR hazard_detector_2 (
    .REG_DEST(d_e_reg_1_e_rt), .REG_SRC(f_d_reg_1_d_inst[20:16]), .REG_WRITE(ctrdreg_1_memtorege),
    .IS_HAZARD(hazard_detector_2_is_hazard));
  OP_Decode op_decode_1 (
    .OP3(f_d_reg_1_d_inst[29]), .OP2(f_d_reg_1_d_inst[28]), .OP1(f_d_reg_1_d_inst[27]),
    .OP0(f_d_reg_1_d_inst[26]), .OP5(f_d_reg_1_d_inst[31]), .OP4(f_d_reg_1_d_inst[30]),
    .out_13(op_decode_1_out_13), .out_15(op_decode_1_out_15), .out_17(op_decode_1_out_17),
    .out_19(op_decode_1_out_19), .out_9(op_decode_1_out_9), .out_11(op_decode_1_out_11),
    .ALU_SRC(op_decode_1_alu_src), .REG_DST(op_decode_1_reg_dst), .REG_WRITE(op_decode_1_reg_write),
    .JUMP(op_decode_1_jump), .ALU_OP(op_decode_1_alu_op), .MEM_2REG(op_decode_1_mem_2reg),
    .MEM_WRITE(op_decode_1_mem_write), .BRANCH(op_decode_1_branch));
  ALU_Decode alu_decode_1 (
    .in_2(op_decode_1_out_9), .in_3(op_decode_1_out_11), .in_4(op_decode_1_out_13),
    .in_5(op_decode_1_out_15), .in_6(op_decode_1_out_17), .in_7(op_decode_1_out_19),
    .ALU_OP(op_decode_1_alu_op), .F0(f_d_reg_1_d_inst[0]), .F1(f_d_reg_1_d_inst[1]),
    .F2(f_d_reg_1_d_inst[2]), .F3(f_d_reg_1_d_inst[3]), .F4(f_d_reg_1_d_inst[4]), .F5(f_d_reg_1_d_inst[5]),
    .ALU_CTRL(alu_decode_1_alu_ctrl));
  RegFile regfile_1 (
    .WE3(ctrwreg_1_regwritew), .R(RESET_out), .CLK(clock_1_out), .A3(m_w_reg_1_w_write_reg),
    .A1(f_d_reg_1_d_inst[25:21]), .A2(f_d_reg_1_d_inst[20:16]), .WD3(multiplexer_11_out),
    .RD2(regfile_1_rd2), .RD1(regfile_1_rd1));
  Adder #(.width(32)) adder_2 (.a(f_d_reg_1_d_pcplus4), .b(shifter_1_out), .out(adder_2_out));  // open: cin, cout
  Shifter #(.width(32)) shifter_1 (.in(bit_extender_1_out), .\dist (5'b00010), .out(shifter_1_out));
  ctrDreg ctrdreg_1 (
    .RegWriteD(op_decode_1_reg_write), .MemtoRegD(op_decode_1_mem_2reg), .MemWriteD(op_decode_1_mem_write),
    .BranchD(op_decode_1_branch), .ALUControlD(alu_decode_1_alu_ctrl), .ALUSrcD(op_decode_1_alu_src),
    .RegDstD(op_decode_1_reg_dst), .WE(1'b1), .CLK(clock_1_out), .R(flush_control_1_e),
    .RegWriteE(ctrdreg_1_regwritee), .MemtoRegE(ctrdreg_1_memtorege), .MemWriteE(ctrdreg_1_memwritee),
    .BranchE(ctrdreg_1_branche), .ALUControlE(ctrdreg_1_alucontrole), .ALUScrE(ctrdreg_1_aluscre),
    .RegDstE(ctrdreg_1_regdste));
  D_E_REG d_e_reg_1 (
    .R(flush_control_1_e), .D_RD1(regfile_1_rd1), .D_RD2(regfile_1_rd2), .D_RS(f_d_reg_1_d_inst[25:21]),
    .D_RT(f_d_reg_1_d_inst[20:16]), .D_RD(f_d_reg_1_d_inst[15:11]), .D_SIGN_IMM(bit_extender_1_out),
    .D_PC4(adder_2_out), .we(1'b1), .CLK(clock_1_out), .E_RD1(d_e_reg_1_e_rd1), .E_RD2(d_e_reg_1_e_rd2),
    .E_RS(d_e_reg_1_e_rs), .E_RT(d_e_reg_1_e_rt), .E_RD(d_e_reg_1_e_rd), .E_SIGN_IMM(d_e_reg_1_e_sign_imm),
    .E_PC4(d_e_reg_1_e_pc4));
  Multiplexer #(.width(5)) multiplexer_3 (
    .in0(d_e_reg_1_e_rt), .in1(d_e_reg_1_e_rd), .out(multiplexer_3_out), .sel(ctrdreg_1_regdste));
  Multiplexer #(.select(2), .width(32)) multiplexer_4 (
    .in0(d_e_reg_1_e_rd1), .in1(multiplexer_11_out), .in2(e_m_reg_1_m_alu_out), .out(multiplexer_4_out),
    .sel(multiplexer_7_out));  // open: in3
  Multiplexer #(.select(2), .width(32)) multiplexer_5 (
    .in0(d_e_reg_1_e_rd2), .in1(multiplexer_11_out), .in2(e_m_reg_1_m_alu_out), .out(multiplexer_5_out),
    .sel(multiplexer_8_out));  // open: in3
  Multiplexer #(.width(32)) multiplexer_6 (
    .in0(multiplexer_5_out), .in1(d_e_reg_1_e_sign_imm), .out(multiplexer_6_out), .sel(ctrdreg_1_aluscre));
  and and_1 (and_1_out, ctrdreg_1_branche, alu_2_1_equal);
  ALU_2 alu_2_1 (
    .CLK(clock_1_out), .R(flush_control_1_out_8), .AluOP(ctrdreg_1_alucontrole), .A(multiplexer_4_out),
    .B(multiplexer_6_out), .RESULT(alu_2_1_result), .SIGNED_OVERFLOW(alu_2_1_signed_overflow),
    .EQUAL(alu_2_1_equal));  // open: UNSIGNED_OVERFLOW
  Multiplexer #(.width(2)) multiplexer_7 (
    .in0(multiplexer_9_out), .in1(2'b10), .out(multiplexer_7_out), .sel(hazard_detector_4_is_hazard));
  Multiplexer #(.width(2)) multiplexer_8 (
    .in0(multiplexer_10_out), .in1(2'b10), .out(multiplexer_8_out), .sel(hazard_detector_6_is_hazard));
  and and_2 (and_2_out, ctrdreg_1_regwritee, ~alu_2_1_signed_overflow);  // AND_Gate
  Multiplexer #(.width(2)) multiplexer_9 (
    .in0(2'b00), .in1(2'b01), .out(multiplexer_9_out), .sel(hazard_detector_3_is_hazard));
  Multiplexer #(.width(2)) multiplexer_10 (
    .in0(2'b00), .in1(2'b01), .out(multiplexer_10_out), .sel(hazard_detector_5_is_hazard));
  ctrEreg ctrereg_1 (
    .RegWriteE(and_2_out), .MemtoRegE(ctrdreg_1_memtorege), .MemWriteE(ctrdreg_1_memwritee),
    .WE(e_m_reg_1_we1), .CLK(clock_1_out), .R(e_m_reg_1_r1), .CLK1(ctrereg_1_clk1),
    .RegWriteM(ctrereg_1_regwritem), .MemtoRegM(ctrereg_1_memtoregm), .MemWriteM(ctrereg_1_memwritem));  // open: BranchE, BranchM
  E_M_REG e_m_reg_1 (
    .E_ALU_OUT(alu_2_1_result), .E_WRITE_DATA(multiplexer_5_out), .E_WRITE_REG(multiplexer_3_out),
    .R(flush_control_1_out_8), .WE(1'b1), .CLK(ctrereg_1_clk1), .R1(e_m_reg_1_r1), .WE1(e_m_reg_1_we1),
    .M_ALU_OUT(e_m_reg_1_m_alu_out), .M_WRITE_DATA(e_m_reg_1_m_write_data),
    .M_WRITE_REG(e_m_reg_1_m_write_reg));  // open: E_EQ, E_PC_BRANCH, M_EQ, M_PC_BRANCH
  HAZARD_DETECTOR hazard_detector_3 (
    .REG_DEST(m_w_reg_1_w_write_reg), .REG_SRC(d_e_reg_1_e_rs), .REG_WRITE(ctrwreg_1_regwritew),
    .IS_HAZARD(hazard_detector_3_is_hazard));
  HAZARD_DETECTOR hazard_detector_4 (
    .REG_DEST(e_m_reg_1_m_write_reg), .REG_SRC(d_e_reg_1_e_rs), .REG_WRITE(ctrereg_1_regwritem),
    .IS_HAZARD(hazard_detector_4_is_hazard));
  HAZARD_DETECTOR hazard_detector_5 (
    .REG_DEST(m_w_reg_1_w_write_reg), .REG_SRC(d_e_reg_1_e_rt), .REG_WRITE(ctrwreg_1_regwritew),
    .IS_HAZARD(hazard_detector_5_is_hazard));
  HAZARD_DETECTOR hazard_detector_6 (
    .REG_DEST(e_m_reg_1_m_write_reg), .REG_SRC(d_e_reg_1_e_rt), .REG_WRITE(ctrereg_1_regwritem),
    .IS_HAZARD(hazard_detector_6_is_hazard));
  // RAM #(.addrWidth(24), .enables("line"), .line("quad"), .\type ("nonvolatile")) ram_1: pin names not known; wires that end beside it: e_m_reg_1_m_alu_out[23:0], ctrereg_1_memwritem, ctrereg_1_memwritem, ctrereg_1_memwritem, ctrereg_1_memwritem, ctrereg_1_memwritem, clock_1_out, e_m_reg_1_m_write_data[31:24], e_m_reg_1_m_write_data[23:16], e_m_reg_1_m_write_data[15:8], e_m_reg_1_m_write_data[7:0], ram_1_p12, ram_1_p13, ram_1_p14, ram_1_p15
  ctrWreg ctrwreg_1 (
    .RegWriteM(ctrereg_1_regwritem), .MemtoRegM(ctrereg_1_memtoregm), .WE(m_w_reg_1_we1), .CLK(clock_1_out),
    .R(m_w_reg_1_r1), .CLK1(ctrwreg_1_clk1), .RegWriteW(ctrwreg_1_regwritew), .MemtoRegW(ctrwreg_1_memtoregw));
  M_W_REG m_w_reg_1 (
    .M_RD(e_m_reg_1_m_alu_out), .M_ALU_OUT({ram_1_p12, ram_1_p13, ram_1_p14, ram_1_p15}),
    .M_WRITE_REG(e_m_reg_1_m_write_reg), .R(flush_control_1_out_8), .WE(1'b1), .CLK(ctrwreg_1_clk1),
    .R1(m_w_reg_1_r1), .WE1(m_w_reg_1_we1), .W_RD(m_w_reg_1_w_rd), .W_ALU_OUT(m_w_reg_1_w_alu_out),
    .W_WRITE_REG(m_w_reg_1_w_write_reg));
  Multiplexer #(.width(32)) multiplexer_11 (
    .in0(m_w_reg_1_w_rd), .in1(m_w_reg_1_w_alu_out), .out(multiplexer_11_out), .sel(ctrwreg_1_memtoregw));

  // Notes on the sheet:
  //   drop 32:24
  //   contents of rom_1 (hex, n*v repeats v):
  //   20 12 0 5 20 13 0 c 22 77 ff f7 2 f2 a0 25 2 74 a8 24 2 b4 a8 20 12 f5 0 a 2 74 a0 2a 10 14 0 1 20
  //   15 0 0 2 f2 a0 2a 2 95 b8 20 2 f2 b8 22 ae 77 0 44 8c 12 0 50 8 0 0 11 20 12 0 1 ac 12 0 54
  //   AND WRITE SIGNAL WITH ~OF FLAG IN EX so overflowed does not get written
endmodule

module RegFile (
  input  WE3,
  input  [4:0] A3,
  input  R,
  input  CLK,
  input  [4:0] A1,
  input  [4:0] A2,
  input  [31:0] WD3,
  output [31:0] RD1,
  output [31:0] RD2
);

  wire not_1_out;
  wire [7:0] decoder_1_out0, decoder_1_out8, decoder_1_out16, decoder_1_out24;
  wire [31:0] a0_4_q, a1_5_q, a2_6_q, a3_7_q, at_1_q, fp_30_q, gp_28_q, k0_26_q, k1_27_q, ra_31_q, s0_16_q,
       s1_17_q, s2_18_q, s3_19_q, s4_20_q, s5_21_q, s6_22_q, s7_23_q, sp_29_q, t0_8_q, t1_9_q, t2_10_q,
       t3_11_q, t4_12_q, t5_13_q, t6_14_q, t7_15_q, t8_24_q, t9_25_q, v0_2_q, v1_3_q, zero_0_q;

  Decoder #(.select(5)) decoder_1 (
    .out0(decoder_1_out0[0]), .out1(decoder_1_out0[1]), .out2(decoder_1_out0[2]), .out3(decoder_1_out0[3]),
    .out4(decoder_1_out0[4]), .out5(decoder_1_out0[5]), .out6(decoder_1_out0[6]), .out7(decoder_1_out0[7]),
    .out8(decoder_1_out8[0]), .out9(decoder_1_out8[1]), .out10(decoder_1_out8[2]), .out11(decoder_1_out8[3]),
    .out12(decoder_1_out8[4]), .out13(decoder_1_out8[5]), .out14(decoder_1_out8[6]),
    .out15(decoder_1_out8[7]), .out16(decoder_1_out16[0]), .out17(decoder_1_out16[1]),
    .out18(decoder_1_out16[2]), .out19(decoder_1_out16[3]), .out20(decoder_1_out16[4]),
    .out21(decoder_1_out16[5]), .out22(decoder_1_out16[6]), .out23(decoder_1_out16[7]),
    .out24(decoder_1_out24[0]), .out25(decoder_1_out24[1]), .out26(decoder_1_out24[2]),
    .out27(decoder_1_out24[3]), .out28(decoder_1_out24[4]), .out29(decoder_1_out24[5]),
    .out30(decoder_1_out24[6]), .out31(decoder_1_out24[7]), .sel(A3), .en(WE3));
  not not_1 (not_1_out, CLK);
  Multiplexer #(.select(5), .width(32)) multiplexer_1 (
    .in0(zero_0_q), .in1(at_1_q), .in2(v0_2_q), .in3(v1_3_q), .in4(a0_4_q), .in5(a1_5_q), .in6(a2_6_q),
    .in7(a3_7_q), .in8(t0_8_q), .in9(t1_9_q), .in10(t2_10_q), .in11(t3_11_q), .in12(t4_12_q), .in13(t5_13_q),
    .in14(t6_14_q), .in15(t7_15_q), .in16(s0_16_q), .in17(s1_17_q), .in18(s2_18_q), .in19(s3_19_q),
    .in20(s4_20_q), .in21(s5_21_q), .in22(s6_22_q), .in23(s7_23_q), .in24(t8_24_q), .in25(t9_25_q),
    .in26(k0_26_q), .in27(k1_27_q), .in28(gp_28_q), .in29(sp_29_q), .in30(fp_30_q), .in31(ra_31_q),
    .out(RD1), .sel(A1));
  Register #(.width(32)) zero_0 (.D(WD3), .clk(not_1_out), .Q(zero_0_q), .clr(1'b1));  // open: en
  Register #(.width(32)) t0_8 (.D(WD3), .en(decoder_1_out8[0]), .clk(not_1_out), .Q(t0_8_q), .clr(R));
  Register #(.width(32)) s0_16 (.D(WD3), .en(decoder_1_out16[0]), .clk(not_1_out), .Q(s0_16_q), .clr(R));
  Register #(.width(32)) t8_24 (.D(WD3), .en(decoder_1_out24[0]), .clk(not_1_out), .Q(t8_24_q), .clr(R));
  Register #(.width(32)) at_1 (.D(WD3), .en(decoder_1_out0[1]), .clk(not_1_out), .Q(at_1_q), .clr(R));
  Register #(.width(32)) t1_9 (.D(WD3), .en(decoder_1_out8[1]), .clk(not_1_out), .Q(t1_9_q), .clr(R));
  Register #(.width(32)) s1_17 (.D(WD3), .en(decoder_1_out16[1]), .clk(not_1_out), .Q(s1_17_q), .clr(R));
  Register #(.width(32)) t9_25 (.D(WD3), .en(decoder_1_out24[1]), .clk(not_1_out), .Q(t9_25_q), .clr(R));
  Register #(.width(32)) v0_2 (.D(WD3), .en(decoder_1_out0[2]), .clk(not_1_out), .Q(v0_2_q), .clr(R));
  Register #(.width(32)) t2_10 (.D(WD3), .en(decoder_1_out8[2]), .clk(not_1_out), .Q(t2_10_q), .clr(R));
  Register #(.width(32)) s2_18 (.D(WD3), .en(decoder_1_out16[2]), .clk(not_1_out), .Q(s2_18_q), .clr(R));
  Register #(.width(32)) k0_26 (.D(WD3), .en(decoder_1_out24[2]), .clk(not_1_out), .Q(k0_26_q), .clr(R));
  Register #(.width(32)) v1_3 (.D(WD3), .en(decoder_1_out0[3]), .clk(not_1_out), .Q(v1_3_q), .clr(R));
  Register #(.width(32)) t3_11 (.D(WD3), .en(decoder_1_out8[3]), .clk(not_1_out), .Q(t3_11_q), .clr(R));
  Register #(.width(32)) s3_19 (.D(WD3), .en(decoder_1_out16[3]), .clk(not_1_out), .Q(s3_19_q), .clr(R));
  Register #(.width(32)) k1_27 (.D(WD3), .en(decoder_1_out24[3]), .clk(not_1_out), .Q(k1_27_q), .clr(R));
  Register #(.width(32)) a0_4 (.D(WD3), .en(decoder_1_out0[4]), .clk(not_1_out), .Q(a0_4_q), .clr(R));
  Register #(.width(32)) t4_12 (.D(WD3), .en(decoder_1_out8[4]), .clk(not_1_out), .Q(t4_12_q), .clr(R));
  Register #(.width(32)) s4_20 (.D(WD3), .en(decoder_1_out16[4]), .clk(not_1_out), .Q(s4_20_q), .clr(R));
  Register #(.width(32)) gp_28 (.D(WD3), .en(decoder_1_out24[4]), .clk(not_1_out), .Q(gp_28_q), .clr(R));
  Register #(.width(32)) a1_5 (.D(WD3), .en(decoder_1_out0[5]), .clk(not_1_out), .Q(a1_5_q), .clr(R));
  Register #(.width(32)) t5_13 (.D(WD3), .en(decoder_1_out8[5]), .clk(not_1_out), .Q(t5_13_q), .clr(R));
  Register #(.width(32)) s5_21 (.D(WD3), .en(decoder_1_out16[5]), .clk(not_1_out), .Q(s5_21_q), .clr(R));
  Register #(.width(32)) sp_29 (.D(WD3), .en(decoder_1_out24[5]), .clk(not_1_out), .Q(sp_29_q), .clr(R));
  Register #(.width(32)) a2_6 (.D(WD3), .en(decoder_1_out0[6]), .clk(not_1_out), .Q(a2_6_q), .clr(R));
  Register #(.width(32)) t6_14 (.D(WD3), .en(decoder_1_out8[6]), .clk(not_1_out), .Q(t6_14_q), .clr(R));
  Register #(.width(32)) s6_22 (.D(WD3), .en(decoder_1_out16[6]), .clk(not_1_out), .Q(s6_22_q), .clr(R));
  Register #(.width(32)) fp_30 (.D(WD3), .en(decoder_1_out24[6]), .clk(not_1_out), .Q(fp_30_q), .clr(R));
  Register #(.width(32)) a3_7 (.D(WD3), .en(decoder_1_out0[7]), .clk(not_1_out), .Q(a3_7_q), .clr(R));
  Register #(.width(32)) t7_15 (.D(WD3), .en(decoder_1_out8[7]), .clk(not_1_out), .Q(t7_15_q), .clr(R));
  Register #(.width(32)) s7_23 (.D(WD3), .en(decoder_1_out16[7]), .clk(not_1_out), .Q(s7_23_q), .clr(R));
  Register #(.width(32)) ra_31 (.D(WD3), .en(decoder_1_out24[7]), .clk(not_1_out), .Q(ra_31_q), .clr(R));
  Multiplexer #(.select(5), .width(32)) multiplexer_2 (
    .in0(zero_0_q), .in1(at_1_q), .in2(v0_2_q), .in3(v1_3_q), .in4(a0_4_q), .in5(a1_5_q), .in6(a2_6_q),
    .in7(a3_7_q), .in8(t0_8_q), .in9(t1_9_q), .in10(t2_10_q), .in11(t3_11_q), .in12(t4_12_q), .in13(t5_13_q),
    .in14(t6_14_q), .in15(t7_15_q), .in16(s0_16_q), .in17(s1_17_q), .in18(s2_18_q), .in19(s3_19_q),
    .in20(s4_20_q), .in21(s5_21_q), .in22(s6_22_q), .in23(s7_23_q), .in24(t8_24_q), .in25(t9_25_q),
    .in26(k0_26_q), .in27(k1_27_q), .in28(gp_28_q), .in29(sp_29_q), .in30(fp_30_q), .in31(ra_31_q),
    .out(RD2), .sel(A2));

  // Notes on the sheet:
  //   RD2: pull=down
  //   WD3: pull=down
  //   RD1: pull=down
endmodule

module ALU (
  input  [3:0] AluOP,
  input  [31:0] X,
  input  [31:0] Y,
  output SIGNED_OVERFLOW,
  output UNSIGNED_OVERFLOW,
  output EQUAL,
  output [31:0] RESULT,
  output [31:0] RESULT_2
);

  wire comparator_1_lt, comparator_2_lt;
  wire [1:0] add_1_cf, sub_1_cf;
  wire [31:0] add_1_result, and_1_out, bit_extender_1_out, bit_extender_2_out, divider_1_out, divider_1_rem,
       multiplier_1_cout, multiplier_1_out, not_1_out, or_1_out, or_2_out, shifter_1_out, shifter_2_out,
       shifter_3_out, sub_1_result, xor_1_out;

  Shifter #(.width(32)) shifter_1 (.in(X), .\dist (Y[4:0]), .out(shifter_1_out));
  Shifter #(.shift("ar"), .width(32)) shifter_2 (.in(X), .\dist (Y[4:0]), .out(shifter_2_out));
  Shifter #(.shift("lr"), .width(32)) shifter_3 (.in(X), .\dist (Y[4:0]), .out(shifter_3_out));
  Multiplier #(.width(32)) multiplier_1 (.a(X), .b(Y), .out(multiplier_1_out), .cout(multiplier_1_cout));  // open: cin
  Divider #(.width(32)) divider_1 (.a(X), .b(Y), .out(divider_1_out), .rem(divider_1_rem));  // open: upper
  ADD add_1 (.X(X), .Y(Y), .CF(add_1_cf[0]), .OF(add_1_cf[1]), .RESULT(add_1_result));  // open: CIN
  SUB sub_1 (.X(X), .Y(Y), .CF(sub_1_cf[0]), .OF(sub_1_cf[1]), .RESULT(sub_1_result));  // open: BIN
  assign and_1_out = X & Y;  // AND_Gate and_1, 32 bits wide
  assign or_1_out = X | Y;  // OR_Gate or_1, 32 bits wide
  assign xor_1_out = X ^ Y;  // XOR_Gate xor_1, 32 bits wide
  assign or_2_out = X | Y;  // OR_Gate or_2, 32 bits wide
  Comparator #(.width(32)) comparator_1 (.a(X), .b(Y), .lt(comparator_1_lt));  // open: gt, eq
  Comparator #(.mode("unsigned"), .width(32)) comparator_2 (
    .a(X), .b(Y), .eq(EQUAL), .lt(comparator_2_lt));  // open: gt
  assign not_1_out = ~or_2_out;  // NOT_Gate not_1, 32 bits wide
  Multiplexer #(.select(4), .width(2)) multiplexer_1 (
    .in0(2'b00), .in1(2'b00), .in2(2'b00), .in3(2'b00), .in4(2'b00), .in5(add_1_cf), .in6(sub_1_cf),
    .in7(2'b00), .in8(2'b00), .in9(2'b00), .in10(2'b00), .in11(2'b00), .in12(2'b00), .in13(2'b00),
    .in14(2'b00), .in15(2'b00), .out({SIGNED_OVERFLOW, UNSIGNED_OVERFLOW}), .sel(AluOP));
  assign bit_extender_1_out = {{31{1'b0}}, comparator_1_lt};  // Bit_Extender bit_extender_1
  assign bit_extender_2_out = {{31{1'b0}}, comparator_2_lt};  // Bit_Extender bit_extender_2
  Multiplexer #(.select(4), .width(32)) multiplexer_2 (
    .in0({32{1'b0}}), .in1({32{1'b0}}), .in2({32{1'b0}}), .in3(multiplier_1_cout), .in4(divider_1_rem),
    .in5({32{1'b0}}), .in6({32{1'b0}}), .in7({32{1'b0}}), .in8({32{1'b0}}), .in9({32{1'b0}}),
    .in10({32{1'b0}}), .in11({32{1'b0}}), .in12({32{1'b0}}), .in13({32{1'b0}}), .in14({32{1'b0}}),
    .in15({32{1'b0}}), .out(RESULT_2), .sel(AluOP));
  Multiplexer #(.select(4), .width(32)) multiplexer_3 (
    .in0(shifter_1_out), .in1(shifter_2_out), .in2(shifter_3_out), .in3(multiplier_1_out),
    .in4(divider_1_out), .in5(add_1_result), .in6(sub_1_result), .in7(and_1_out), .in8(or_1_out),
    .in9(xor_1_out), .in10(not_1_out), .in11(bit_extender_1_out), .in12(bit_extender_2_out),
    .in13({32{1'b0}}), .in14({32{1'b0}}), .in15({32{1'b0}}), .out(RESULT), .sel(AluOP));

  // Other names for the same wires on the sheet: CF = UNSIGNED_OVERFLOW; OF = SIGNED_OVERFLOW;
  //   Result2[31:0] = RESULT_2; S[3:0] = AluOP
endmodule

module ADD (
  input  [31:0] X,
  input  CIN,
  input  [31:0] Y,
  output [31:0] RESULT,
  output CF,
  output OF
);

  wire adder_1_cout;

  Adder #(.width(31)) adder_1 (.a(X[30:0]), .b(Y[30:0]), .out(RESULT[30:0]), .cin(CIN), .cout(adder_1_cout));
  Adder #(.width(1)) adder_2 (.a(X[31]), .b(Y[31]), .out(RESULT[31]), .cin(adder_1_cout), .cout(CF));
  xor xor_1 (OF, adder_1_cout, CF);
endmodule

module SUB (
  input  [31:0] X,
  input  BIN,
  input  [31:0] Y,
  output [31:0] RESULT,
  output CF,
  output OF
);

  wire subtractor_1_bout;

  Subtractor #(.width(31)) subtractor_1 (
    .a(X[30:0]), .b(Y[30:0]), .out(RESULT[30:0]), .bin(BIN), .bout(subtractor_1_bout));
  Subtractor #(.width(1)) subtractor_2 (.a(X[31]), .b(Y[31]), .out(RESULT[31]), .bin(subtractor_1_bout), .bout(CF));
  xor xor_1 (OF, subtractor_1_bout, CF);
endmodule

module OP_Decode (
  input  OP5,
  input  OP4,
  input  OP3,
  input  OP2,
  input  OP1,
  input  OP0,
  output [1:0] ALU_OP,
  output MEM_2REG,
  output out_9,
  output MEM_WRITE,
  output out_11,
  output BRANCH,
  output out_13,
  output ALU_SRC,
  output out_15,
  output REG_DST,
  output out_17,
  output REG_WRITE,
  output out_19,
  output JUMP
);

  wire and_1_out, and_2_out, and_3_out, and_4_out, and_5_out, and_6_out, and_7_out, undriven, undriven_2,
       undriven_3, undriven_4, undriven_5, undriven_6;
  wire [7:0] controlled_buffer_7_out, pull_resistor_8_node;
  wire [8:0] pull_resistor_1_node, pull_resistor_2_node, pull_resistor_3_node, pull_resistor_5_node,
       pull_resistor_6_node;
  wire [8:1] pull_resistor_4_node;

  assign {JUMP, REG_WRITE, REG_DST, ALU_SRC, BRANCH, MEM_WRITE, MEM_2REG, ALU_OP} = and_1_out ? {pull_resistor_1_node[8:7], pull_resistor_1_node[7], pull_resistor_1_node[5:2], pull_resistor_1_node[7], pull_resistor_1_node[0]} : 9'bz;  // Controlled_Buffer controlled_buffer_1
  and and_1 (and_1_out, ~OP5, ~OP4, ~OP3, ~OP2, ~OP1, ~OP0);  // AND_Gate
  Pull_Resistor pull_resistor_1 (.node({pull_resistor_1_node[8:7], pull_resistor_1_node[7], pull_resistor_1_node[5:2], pull_resistor_1_node[7], pull_resistor_1_node[0]}));
  assign {JUMP, REG_WRITE, REG_DST, ALU_SRC, BRANCH, MEM_WRITE, MEM_2REG, ALU_OP} = and_2_out ? {pull_resistor_2_node[8:6], pull_resistor_2_node[7], pull_resistor_2_node[4:3], pull_resistor_2_node[7], pull_resistor_2_node[1:0]} : 9'bz;  // Controlled_Buffer controlled_buffer_2
  and and_2 (and_2_out, OP5, ~OP4, ~OP3, ~OP2, OP1, OP0);  // AND_Gate
  Pull_Resistor pull_resistor_2 (.node({pull_resistor_2_node[8:6], pull_resistor_2_node[7], pull_resistor_2_node[4:3], pull_resistor_2_node[7], pull_resistor_2_node[1:0]}));
  assign {JUMP, REG_WRITE, REG_DST, ALU_SRC, BRANCH, MEM_WRITE, MEM_2REG, ALU_OP} = and_3_out ? {pull_resistor_3_node[8:4], pull_resistor_3_node[5], pull_resistor_3_node[2:0]} : 9'bz;  // Controlled_Buffer controlled_buffer_3
  and and_3 (and_3_out, OP5, ~OP4, OP3, ~OP2, OP1, OP0);  // AND_Gate
  Pull_Resistor pull_resistor_3 (.node({pull_resistor_3_node[8:4], pull_resistor_3_node[5], pull_resistor_3_node[2:0]}));
  assign {JUMP, REG_WRITE, REG_DST, ALU_SRC, BRANCH, MEM_WRITE, MEM_2REG, ALU_OP} = and_4_out ? {pull_resistor_4_node, pull_resistor_4_node[4]} : 9'bz;  // Controlled_Buffer controlled_buffer_4
  and and_4 (and_4_out, ~OP5, ~OP4, ~OP3, OP2, ~OP1, ~OP0);  // AND_Gate
  Pull_Resistor pull_resistor_4 (.node({pull_resistor_4_node, pull_resistor_4_node[4]}));
  assign {JUMP, REG_WRITE, REG_DST, ALU_SRC, BRANCH, MEM_WRITE, MEM_2REG, ALU_OP} = and_5_out ? {pull_resistor_5_node[8:6], pull_resistor_5_node[7], pull_resistor_5_node[4:0]} : 9'bz;  // Controlled_Buffer controlled_buffer_5
  and and_5 (and_5_out, ~OP5, ~OP4, OP3, ~OP2, ~OP1, ~OP0);  // AND_Gate
  Pull_Resistor pull_resistor_5 (.node({pull_resistor_5_node[8:6], pull_resistor_5_node[7], pull_resistor_5_node[4:0]}));
  assign {JUMP, REG_WRITE, REG_DST, ALU_SRC, BRANCH, MEM_WRITE, MEM_2REG, ALU_OP} = and_6_out ? pull_resistor_6_node : 9'bz;  // Controlled_Buffer controlled_buffer_6
  and and_6 (and_6_out, ~OP5, ~OP4, ~OP3, ~OP2, OP1, ~OP0);  // AND_Gate
  Pull_Resistor pull_resistor_6 (.node(pull_resistor_6_node));
  Pull_Resistor pull_resistor_7 (.node({JUMP, REG_WRITE, REG_DST, ALU_SRC, BRANCH, MEM_WRITE, MEM_2REG, ALU_OP}));
  and and_7 (and_7_out, ~undriven, ~undriven_2, ~undriven_3, ~undriven_4, ~undriven_5, ~undriven_6);  // AND_Gate
  assign controlled_buffer_7_out = and_7_out ? pull_resistor_8_node : 8'bz;  // Controlled_Buffer controlled_buffer_7
  Pull_Resistor pull_resistor_8 (.node(pull_resistor_8_node));

  assign out_9 = OP5;
  assign out_11 = OP4;
  assign out_13 = OP3;
  assign out_15 = OP2;
  assign out_17 = OP1;
  assign out_19 = OP0;
  // also tied to VCC on the sheet: {pull_resistor_1_node[7], pull_resistor_2_node[7], pull_resistor_3_node[5], pull_resistor_4_node[4], pull_resistor_5_node[7], pull_resistor_6_node[8]}

  // Notes on the sheet:
  //   R_TYPE
  //   LW
  //   SW
  //   BEQ
  //   ADDI
  //   JUMP
endmodule

module ALU_Decode (
  input  [1:0] ALU_OP,
  input  in_2,
  input  in_3,
  input  in_4,
  input  in_5,
  input  in_6,
  input  in_7,
  input  F0,
  input  F1,
  input  F2,
  input  F3,
  input  F4,
  input  F5,
  output [4:0] ALU_CTRL
);

  wire and_1_out, and_2_out, and_3_out, and_4_out, and_5_out, and_6_out, and_7_out, and_8_out, and_9_out,
       and_10_out, and_11_out, and_12_out, and_13_out, and_14_out, and_15_out, and_16_out, and_17_out,
       and_18_out, and_19_out, and_20_out, and_21_out, and_22_out, and_23_out, and_24_out, and_25_out,
       and_26_out, and_27_out, and_28_out, and_29_out, and_30_out, and_31_out, and_32_out, and_33_out,
       and_34_out, and_35_out, and_36_out, and_37_out, and_38_out, and_39_out, and_40_out, and_41_out,
       and_42_out, and_43_out, and_44_out, and_45_out, undriven, undriven_2, undriven_3, undriven_4,
       undriven_5, undriven_6;
  wire [4:0] or_1_out, pull_resistor_1_node;

  and and_1 (and_1_out, ~in_2, ~in_3, ~in_4, ~in_5, ~in_6, ~in_7);  // AND_Gate
  and and_2 (and_2_out, F0, F1, ~F2, ~F3, ~F4, ~F5);  // AND_Gate
  and and_3 (and_3_out, F0, F1, F2, ~F3, ~F4, ~F5);  // AND_Gate
  and and_4 (and_4_out, ~F0, F1, ~F2, F3, F4, ~F5);  // AND_Gate
  and and_5 (and_5_out, ~F0, ~F1, ~F2, ~F3, F4, ~F5);  // AND_Gate
  and and_6 (and_6_out, F0, ~F1, ~F2, ~F3, F4, ~F5);  // AND_Gate
  and and_7 (and_7_out, ~F0, ~F1, ~F2, F3, F4, ~F5);  // AND_Gate
  and and_8 (and_8_out, ~F0, ~F1, ~F2, ~F3, ~F4, F5);  // AND_Gate
  and and_9 (and_9_out, ~F0, ~F1, F2, ~F3, ~F4, F5);  // AND_Gate
  and and_10 (and_10_out, F0, ~F1, F2, ~F3, ~F4, F5);  // AND_Gate
  and and_11 (and_11_out, F0, F1, ~F2, F3, ~F4, F5);  // AND_Gate
  and and_12 (and_12_out, F0, F1, ~F2, ~F3, ~F4, F5);  // AND_Gate
  and and_13 (and_13_out, ~F0, F1, ~F2, ~F3, ~F4, ~F5);  // AND_Gate
  and and_14 (and_14_out, ~F0, F1, F2, ~F3, ~F4, ~F5);  // AND_Gate
  and and_15 (and_15_out, ~F0, F1, ~F2, F3, F4, ~F5);  // AND_Gate
  and and_16 (and_16_out, ~F0, F1, ~F2, ~F3, F4, ~F5);  // AND_Gate
  and and_17 (and_17_out, F0, ~F1, ~F2, ~F3, F4, ~F5);  // AND_Gate
  and and_18 (and_18_out, F0, ~F1, ~F2, F3, F4, ~F5);  // AND_Gate
  and and_19 (and_19_out, ~F0, ~F1, ~F2, ~F3, ~F4, F5);  // AND_Gate
  and and_20 (and_20_out, F0, F1, F2, ~F3, ~F4, F5);  // AND_Gate
  and and_21 (and_21_out, F0, ~F1, F2, ~F3, ~F4, F5);  // AND_Gate
  and and_22 (and_22_out, ~F0, F1, ~F2, ~F3, ~F4, F5);  // AND_Gate
  and and_23 (and_23_out, F0, F1, ~F2, ~F3, ~F4, F5);  // AND_Gate
  and and_24 (and_24_out, F0, F1, ~F2, F3, F4, ~F5);  // AND_Gate
  and and_25 (and_25_out, ~F0, ~F1, ~F2, ~F3, F4, ~F5);  // AND_Gate
  and and_26 (and_26_out, ~F0, F1, ~F2, ~F3, F4, ~F5);  // AND_Gate
  and and_27 (and_27_out, F0, ~F1, ~F2, ~F3, F4, ~F5);  // AND_Gate
  and and_28 (and_28_out, F0, ~F1, ~F2, ~F3, ~F4, F5);  // AND_Gate
  and and_29 (and_29_out, ~F0, ~F1, F2, ~F3, ~F4, F5);  // AND_Gate
  and and_30 (and_30_out, F0, F1, F2, ~F3, ~F4, F5);  // AND_Gate
  and and_31 (and_31_out, F0, ~F1, F2, ~F3, ~F4, F5);  // AND_Gate
  and and_32 (and_32_out, ~F0, F1, F2, ~F3, ~F4, F5);  // AND_Gate
  and and_33 (and_33_out, F0, F1, ~F2, ~F3, F4, ~F5);  // AND_Gate
  and and_34 (and_34_out, ~F0, ~F1, ~F2, F3, F4, ~F5);  // AND_Gate
  and and_35 (and_35_out, F0, ~F1, ~F2, F3, F4, ~F5);  // AND_Gate
  and and_36 (and_36_out, ~F0, ~F1, ~F2, ~F3, ~F4, F5);  // AND_Gate
  and and_37 (and_37_out, F0, ~F1, ~F2, ~F3, ~F4, F5);  // AND_Gate
  and and_38 (and_38_out, ~F0, ~F1, F2, ~F3, ~F4, F5);  // AND_Gate
  and and_39 (and_39_out, F0, F1, F2, ~F3, ~F4, F5);  // AND_Gate
  and and_40 (and_40_out, F0, ~F1, F2, ~F3, ~F4, F5);  // AND_Gate
  and and_41 (and_41_out, ~F0, F1, ~F2, F3, ~F4, F5);  // AND_Gate
  and and_42 (and_42_out, F0, F1, ~F2, F3, ~F4, F5);  // AND_Gate
  and and_43 (and_43_out, ~F0, F1, ~F2, ~F3, ~F4, F5);  // AND_Gate
  and and_44 (and_44_out, F0, F1, ~F2, ~F3, ~F4, F5);  // AND_Gate
  and and_45 (and_45_out, ~F0, F1, F2, ~F3, ~F4, F5);  // AND_Gate
  Pull_Resistor pull_resistor_1 (.node(pull_resistor_1_node));
  assign pull_resistor_1_node = and_1_out ? or_1_out : 5'bz;  // Controlled_Buffer controlled_buffer_1
  or or_1 (or_1_out[0], and_2_out, and_3_out, and_4_out, and_5_out, and_6_out, and_7_out, and_8_out, and_9_out, and_10_out, and_11_out, and_12_out);
  or or_2 (or_1_out[1], and_13_out, and_14_out, and_15_out, and_16_out, and_17_out, and_18_out, and_19_out, and_20_out, and_21_out, and_22_out, and_23_out);
  or or_3 (or_1_out[2], and_24_out, and_25_out, and_26_out, and_27_out, and_28_out, and_29_out, and_30_out, and_31_out, and_32_out);
  or or_4 (or_1_out[3], and_33_out, and_34_out, and_35_out, and_36_out, and_37_out, and_38_out, and_39_out, and_40_out);
  or or_5 (or_1_out[4], and_41_out, and_42_out, and_43_out, and_44_out, and_45_out);
  Multiplexer #(.select(2), .width(5)) multiplexer_1 (
    .in0(5'b01011), .in1(5'b10010), .in2(pull_resistor_1_node), .out(ALU_CTRL), .sel(ALU_OP));  // open: in3
  // AND_Gate and_46 has open pins: in0=undriven_6, in1=undriven_5, in2=undriven_4, in3=undriven_3, in4=undriven_2, in5=undriven, out=open
  // AND_Gate and_47 has open pins: in0=undriven_6, in1=undriven_5, in2=undriven_4, in3=undriven_3, in4=undriven_2, in5=undriven, out=open
  // AND_Gate and_48 has open pins: in0=undriven_6, in1=undriven_5, in2=undriven_4, in3=undriven_3, in4=undriven_2, in5=undriven, out=open
  // AND_Gate and_49 has open pins: in0=undriven_6, in1=undriven_5, in2=undriven_4, in3=undriven_3, in4=undriven_2, in5=undriven, out=open
  // AND_Gate and_50 has open pins: in0=undriven_6, in1=undriven_5, in2=undriven_4, in3=undriven_3, in4=undriven_2, in5=undriven, out=open
  // AND_Gate and_51 has open pins: in0=undriven_6, in1=undriven_5, in2=undriven_4, in3=undriven_3, in4=undriven_2, in5=undriven, out=open
  // AND_Gate and_52 has open pins: in0=undriven_6, in1=undriven_5, in2=undriven_4, in3=undriven_3, in4=undriven_2, in5=undriven, out=open
  // AND_Gate and_53 has open pins: in0=undriven_6, in1=undriven_5, in2=undriven_4, in3=undriven_3, in4=undriven_2, in5=undriven, out=open
  // AND_Gate and_54 has open pins: in0=undriven_6, in1=undriven_5, in2=undriven_4, in3=undriven_3, in4=undriven_2, in5=undriven, out=open
  // AND_Gate and_55 has open pins: in0=undriven_6, in1=undriven_5, in2=undriven_4, in3=undriven_3, in4=undriven_2, in5=undriven, out=open
  // AND_Gate and_56 has open pins: in0=undriven_6, in1=undriven_5, in2=undriven_4, in3=undriven_3, in4=undriven_2, in5=undriven, out=open
  // AND_Gate and_57 has open pins: in0=undriven_6, in1=undriven_5, in2=undriven_4, in3=undriven_3, in4=undriven_2, in5=undriven, out=open
  // AND_Gate and_58 has open pins: in0=undriven_6, in1=undriven_5, in2=undriven_4, in3=undriven_3, in4=undriven_2, in5=undriven, out=open
  // AND_Gate and_59 has open pins: in0=undriven_6, in1=undriven_5, in2=undriven_4, in3=undriven_3, in4=undriven_2, in5=undriven, out=open
  // AND_Gate and_60 has open pins: in0=undriven_6, in1=undriven_5, in2=undriven_4, in3=undriven_3, in4=undriven_2, in5=undriven, out=open
  // AND_Gate and_61 has open pins: in0=undriven_6, in1=undriven_5, in2=undriven_4, in3=undriven_3, in4=undriven_2, in5=undriven, out=open
  // AND_Gate and_62 has open pins: in0=undriven_6, in1=undriven_5, in2=undriven_4, in3=undriven_3, in4=undriven_2, in5=undriven, out=open
  // AND_Gate and_63 has open pins: in0=undriven_6, in1=undriven_5, in2=undriven_4, in3=undriven_3, in4=undriven_2, in5=undriven, out=open
  // AND_Gate and_64 has open pins: in0=undriven_6, in1=undriven_5, in2=undriven_4, in3=undriven_3, in4=undriven_2, in5=undriven, out=open
  // AND_Gate and_65 has open pins: in0=undriven_6, in1=undriven_5, in2=undriven_4, in3=undriven_3, in4=undriven_2, in5=undriven, out=open
  // AND_Gate and_66 has open pins: in0=undriven_6, in1=undriven_5, in2=undriven_4, in3=undriven_3, in4=undriven_2, in5=undriven, out=open
  // AND_Gate and_67 has open pins: in0=undriven_6, in1=undriven_5, in2=undriven_4, in3=undriven_3, in4=undriven_2, in5=undriven, out=open
  // AND_Gate and_68 has open pins: in0=undriven_6, in1=undriven_5, in2=undriven_4, in3=undriven_3, in4=undriven_2, in5=undriven, out=open
  // AND_Gate and_69 has open pins: in0=undriven_6, in1=undriven_5, in2=undriven_4, in3=undriven_3, in4=undriven_2, in5=undriven, out=open
  // AND_Gate and_70 has open pins: in0=undriven_6, in1=undriven_5, in2=undriven_4, in3=undriven_3, in4=undriven_2, in5=undriven, out=open
  // AND_Gate and_71 has open pins: in0=undriven_6, in1=undriven_5, in2=undriven_4, in3=undriven_3, in4=undriven_2, in5=undriven, out=open
  // AND_Gate and_72 has open pins: in0=undriven_6, in1=undriven_5, in2=undriven_4, in3=undriven_3, in4=undriven_2, in5=undriven, out=open
  // AND_Gate and_73 has open pins: in0=undriven_6, in1=undriven_5, in2=undriven_4, in3=undriven_3, in4=undriven_2, in5=undriven, out=open

  // Notes on the sheet:
  //   SLL
  //   SLLV
  //   SRA
  //   SRAV
  //   SRL
  //   SRLV
  //   DIV
  //   DIVU
  //   MFHI
  //   MFLO
  //   MTHI
  //   MTLO
  //   SYSCALL
  //   MULT
  //   MULTU
  //   BREAK
  //   JALR
  //   JR
  //   ADD
  //   ADDU
  //   AND
  //   NOR
  //   OR
  //   SLT
  //   SLTU
  //   SUB
  //   SUBU
  //   XOR
endmodule

module ctrDreg (
  input  WE,
  input  CLK,
  input  R,
  input  RegWriteD,
  input  MemtoRegD,
  input  MemWriteD,
  input  BranchD,
  input  [4:0] ALUControlD,
  input  ALUSrcD,
  input  RegDstD,
  output RegWriteE,
  output MemtoRegE,
  output MemWriteE,
  output BranchE,
  output [4:0] ALUControlE,
  output ALUScrE,
  output RegDstE
);

  Register #(.width(1)) register_1 (.D(RegWriteD), .en(WE), .clk(CLK), .Q(RegWriteE), .clr(R));
  Register #(.width(1)) register_2 (.D(MemtoRegD), .en(WE), .clk(CLK), .Q(MemtoRegE), .clr(R));
  Register #(.width(1)) register_3 (.D(MemWriteD), .en(WE), .clk(CLK), .Q(MemWriteE), .clr(R));
  Register #(.width(1)) register_4 (.D(BranchD), .en(WE), .clk(CLK), .Q(BranchE), .clr(R));
  Register #(.width(5)) register_5 (.D(ALUControlD), .en(WE), .clk(CLK), .Q(ALUControlE), .clr(R));
  Register #(.width(1)) register_6 (.D(ALUSrcD), .en(WE), .clk(CLK), .Q(ALUScrE), .clr(R));
  Register #(.width(1)) register_7 (.D(RegDstD), .en(WE), .clk(CLK), .Q(RegDstE), .clr(R));
endmodule

module ctrEreg (
  input  WE,
  input  CLK,
  input  R,
  input  RegWriteE,
  input  MemtoRegE,
  input  MemWriteE,
  input  BranchE,
  output CLK1,
  output RegWriteM,
  output MemtoRegM,
  output MemWriteM,
  output BranchM
);

  Register #(.width(1)) register_1 (.D(RegWriteE), .en(WE), .clk(CLK), .Q(RegWriteM), .clr(R));
  Register #(.width(1)) register_2 (.D(MemtoRegE), .en(WE), .clk(CLK), .Q(MemtoRegM), .clr(R));
  Register #(.width(1)) register_3 (.D(MemWriteE), .en(WE), .clk(CLK), .Q(MemWriteM), .clr(R));
  Register #(.width(1)) register_4 (.D(BranchE), .en(WE), .clk(CLK), .Q(BranchM), .clr(R));

  assign CLK1 = CLK;
endmodule

module ctrWreg (
  input  WE,
  input  CLK,
  input  R,
  input  RegWriteM,
  input  MemtoRegM,
  output CLK1,
  output RegWriteW,
  output MemtoRegW
);

  Register #(.width(1)) register_1 (.D(RegWriteM), .en(WE), .clk(CLK), .Q(RegWriteW), .clr(R));
  Register #(.width(1)) register_2 (.D(MemtoRegM), .en(WE), .clk(CLK), .Q(MemtoRegW), .clr(R));

  assign CLK1 = CLK;
endmodule

module D_E_REG (
  input  R,
  input  we,
  input  CLK,
  input  [31:0] D_RD1,
  input  [31:0] D_RD2,
  input  [4:0] D_RS,
  input  [4:0] D_RT,
  input  [4:0] D_RD,
  input  [31:0] D_SIGN_IMM,
  input  [31:0] D_PC4,
  output [31:0] E_RD1,
  output [31:0] E_RD2,
  output [4:0] E_RS,
  output [4:0] E_RT,
  output [4:0] E_RD,
  output [31:0] E_SIGN_IMM,
  output [31:0] E_PC4
);

  wire and_1_out, not_1_out;

  not not_1 (not_1_out, R);
  and and_1 (and_1_out, not_1_out, R);
  Register #(.width(32)) register_1 (.D(D_RD1), .en(we), .clk(CLK), .Q(E_RD1), .clr(and_1_out));
  Register #(.width(32)) register_2 (.D(D_RD2), .en(we), .clk(CLK), .Q(E_RD2), .clr(and_1_out));
  Register #(.width(5)) register_3 (.D(D_RS), .en(we), .clk(CLK), .Q(E_RS), .clr(and_1_out));
  Register #(.width(5)) register_4 (.D(D_RT), .en(we), .clk(CLK), .Q(E_RT), .clr(and_1_out));
  Register #(.width(5)) register_5 (.D(D_RD), .en(we), .clk(CLK), .Q(E_RD), .clr(and_1_out));
  Register #(.width(32)) register_6 (.D(D_SIGN_IMM), .en(we), .clk(CLK), .Q(E_SIGN_IMM), .clr(and_1_out));
  Register #(.width(32)) register_7 (.D(D_PC4), .en(we), .clk(CLK), .Q(E_PC4), .clr(and_1_out));
endmodule

module F_D_REG (
  input  R,
  input  WE,
  input  CLK,
  input  [31:0] Inst,
  input  [31:0] PCplus4,
  output [31:0] D_Inst,
  output [31:0] D_PCplus4
);

  Register #(.width(32)) register_1 (.D(Inst), .en(WE), .clk(CLK), .Q(D_Inst), .clr(R));
  Register #(.width(32)) register_2 (.D(PCplus4), .en(WE), .clk(CLK), .Q(D_PCplus4), .clr(R));
endmodule

module E_M_REG (
  input  R,
  input  WE,
  input  CLK,
  input  E_EQ,
  input  [31:0] E_ALU_OUT,
  input  [31:0] E_WRITE_DATA,
  input  [4:0] E_WRITE_REG,
  input  [31:0] E_PC_BRANCH,
  output R1,
  output WE1,
  output M_EQ,
  output [31:0] M_ALU_OUT,
  output [31:0] M_WRITE_DATA,
  output [4:0] M_WRITE_REG,
  output [31:0] M_PC_BRANCH
);

  Register #(.width(1)) register_1 (.D(E_EQ), .en(WE), .clk(CLK), .Q(M_EQ), .clr(R));
  Register #(.width(32)) register_2 (.D(E_ALU_OUT), .en(WE), .clk(CLK), .Q(M_ALU_OUT), .clr(R));
  Register #(.width(32)) register_3 (.D(E_WRITE_DATA), .en(WE), .clk(CLK), .Q(M_WRITE_DATA), .clr(R));
  Register #(.width(5)) register_4 (.D(E_WRITE_REG), .en(WE), .clk(CLK), .Q(M_WRITE_REG), .clr(R));
  Register #(.width(32)) register_5 (.D(E_PC_BRANCH), .en(WE), .clk(CLK), .Q(M_PC_BRANCH), .clr(R));

  assign R1 = R;
  assign WE1 = WE;
endmodule

module M_W_REG (
  input  R,
  input  WE,
  input  CLK,
  input  [31:0] M_RD,
  input  [31:0] M_ALU_OUT,
  input  [4:0] M_WRITE_REG,
  output R1,
  output WE1,
  output [31:0] W_RD,
  output [31:0] W_ALU_OUT,
  output [4:0] W_WRITE_REG
);

  Register #(.width(32)) register_1 (.D(M_RD), .en(WE), .clk(CLK), .Q(W_RD), .clr(R));
  Register #(.width(32)) register_2 (.D(M_ALU_OUT), .en(WE), .clk(CLK), .Q(W_ALU_OUT), .clr(R));
  Register #(.width(5)) register_3 (.D(M_WRITE_REG), .en(WE), .clk(CLK), .Q(W_WRITE_REG), .clr(R));

  assign R1 = R;
  assign WE1 = WE;
endmodule

module HAZARD_DETECTOR (
  input  REG_WRITE,
  input  [4:0] REG_DEST,
  input  [4:0] REG_SRC,
  output IS_HAZARD
);

  wire comparator_1_eq, or_1_out;

  or or_1 (or_1_out, REG_SRC[0], REG_SRC[1], REG_SRC[2], REG_SRC[3], REG_SRC[4]);
  Comparator #(.width(5)) comparator_1 (.a(REG_DEST), .b(REG_SRC), .eq(comparator_1_eq));  // open: gt, lt
  and and_1 (IS_HAZARD, REG_WRITE, comparator_1_eq, or_1_out);
endmodule

module FLUSH_CONTROL (
  input  R,
  input  J,
  input  B,
  input  CLK,
  input  STALL,
  output D,
  output E,
  output out_8
);

  wire and_1_out, and_2_out, and_3_out, and_4_out, d_ff_1_q, not_1_out, not_2_out, or_1_out, or_4_out;

  not not_1 (not_1_out, CLK);
  and and_1 (and_1_out, not_1_out, CLK);
  or or_1 (or_1_out, J, B);
  or or_2 (D, R, and_2_out);
  and and_2 (and_2_out, or_1_out, and_1_out);
  not not_2 (not_2_out, CLK);
  D_Flip_Flop d_ff_1 (.clk(not_2_out), .D(STALL), .Q(d_ff_1_q));  // open: Qn, preset, reset
  and and_3 (and_3_out, B, and_1_out);
  and and_4 (and_4_out, ~not_2_out, d_ff_1_q);  // AND_Gate
  or or_3 (E, R, or_4_out);
  or or_4 (or_4_out, and_3_out, and_4_out);

  assign out_8 = R;
endmodule

module ALU_2 (
  input  CLK,
  input  R,
  input  [4:0] AluOP,
  input  [31:0] A,
  input  [31:0] B,
  output [31:0] RESULT,
  output SIGNED_OVERFLOW,
  output UNSIGNED_OVERFLOW,
  output EQUAL
);

  wire adder_1_cout, and_2_out, and_3_out, comparator_1_lt, comparator_2_lt, decoder_1_out0, decoder_1_out1,
       decoder_1_out2, decoder_1_out3, decoder_1_out4, decoder_1_out5, decoder_1_out6, decoder_1_out7,
       decoder_1_out8, decoder_1_out9, decoder_1_out10, decoder_1_out11, decoder_1_out12, decoder_1_out13,
       decoder_1_out14, decoder_1_out15, decoder_1_out16, decoder_1_out17, decoder_1_out18, decoder_1_out19,
       decoder_1_out20, or_3_out, subtractor_1_bout;
  wire [1:0] add_1_of, sub_1_of;
  wire [31:0] add_1_result, adder_1_out, and_1_out, bit_extender_1_out, bit_extender_2_out,
       controlled_buffer_1_out, divider_1_out, divider_1_rem, divider_2_out, divider_2_rem, HI_q, LO_q,
       multiplier_1_cout, multiplier_1_out, multiplier_2_cout, multiplier_2_out, not_1_out, or_1_out,
       or_2_out, shifter_1_out, shifter_2_out, shifter_3_out, sub_1_result, subtractor_1_out, xor_1_out;

  Decoder #(.enable("false"), .select(5)) decoder_1 (
    .out0(decoder_1_out0), .out1(decoder_1_out1), .out2(decoder_1_out2), .out3(decoder_1_out3),
    .out4(decoder_1_out4), .out5(decoder_1_out5), .out6(decoder_1_out6), .out7(decoder_1_out7),
    .out8(decoder_1_out8), .out9(decoder_1_out9), .out10(decoder_1_out10), .out11(decoder_1_out11),
    .out12(decoder_1_out12), .out13(decoder_1_out13), .out14(decoder_1_out14), .out15(decoder_1_out15),
    .out16(decoder_1_out16), .out17(decoder_1_out17), .out18(decoder_1_out18), .out19(decoder_1_out19),
    .out20(decoder_1_out20), .sel(AluOP));  // open: out21, out22, out23, out24, out25, out26, out27, out28, out29, out30, out31
  Shifter #(.width(32)) shifter_1 (.in(A), .\dist (B[4:0]), .out(shifter_1_out));
  Shifter #(.shift("ar"), .width(32)) shifter_2 (.in(A), .\dist (B[4:0]), .out(shifter_2_out));
  Shifter #(.shift("lr"), .width(32)) shifter_3 (.in(A), .\dist (B[4:0]), .out(shifter_3_out));
  Divider #(.mode("twosComplement"), .width(32)) divider_1 (
    .a(A), .b(B), .out(divider_1_out), .rem(divider_1_rem));  // open: upper
  Divider #(.width(32)) divider_2 (.a(A), .b(B), .out(divider_2_out), .rem(divider_2_rem));  // open: upper
  Multiplier #(.mode("twosComplement"), .width(32)) multiplier_1 (
    .a(A), .b(B), .out(multiplier_1_out), .cout(multiplier_1_cout));  // open: cin
  Multiplier #(.width(32)) multiplier_2 (.a(A), .b(B), .out(multiplier_2_out), .cout(multiplier_2_cout));  // open: cin
  ADD add_1 (.X(A), .Y(B), .CF(add_1_of[1]), .OF(add_1_of[0]), .RESULT(add_1_result));  // open: CIN
  Adder #(.width(32)) adder_1 (.a(A), .b(B), .out(adder_1_out), .cout(adder_1_cout));  // open: cin
  assign and_1_out = A & B;  // AND_Gate and_1, 32 bits wide
  assign or_1_out = A | B;  // OR_Gate or_1, 32 bits wide
  assign not_1_out = ~or_1_out;  // NOT_Gate not_1, 32 bits wide
  assign or_2_out = A | B;  // OR_Gate or_2, 32 bits wide
  Comparator #(.width(32)) comparator_1 (.a(A), .b(B), .lt(comparator_1_lt));  // open: gt, eq
  Comparator #(.mode("unsigned"), .width(32)) comparator_2 (
    .a(A), .b(B), .eq(EQUAL), .lt(comparator_2_lt));  // open: gt
  SUB sub_1 (.X(A), .Y(B), .CF(sub_1_of[1]), .OF(sub_1_of[0]), .RESULT(sub_1_result));  // open: BIN
  Subtractor #(.width(32)) subtractor_1 (.a(A), .b(B), .out(subtractor_1_out), .bout(subtractor_1_bout));  // open: bin
  assign xor_1_out = A ^ B;  // XOR_Gate xor_1, 32 bits wide
  assign controlled_buffer_1_out = decoder_1_out9 ? multiplier_1_cout : 32'bz;  // Controlled_Buffer controlled_buffer_1
  assign RESULT = decoder_1_out10 ? multiplier_2_out : 32'bz;  // Controlled_Buffer controlled_buffer_2
  assign controlled_buffer_1_out = decoder_1_out10 ? multiplier_2_cout : 32'bz;  // Controlled_Buffer controlled_buffer_3
  assign controlled_buffer_1_out = decoder_1_out3 ? divider_1_rem : 32'bz;  // Controlled_Buffer controlled_buffer_4
  assign RESULT = decoder_1_out4 ? divider_2_out : 32'bz;  // Controlled_Buffer controlled_buffer_5
  assign controlled_buffer_1_out = decoder_1_out4 ? divider_2_rem : 32'bz;  // Controlled_Buffer controlled_buffer_6
  assign controlled_buffer_1_out = decoder_1_out7 ? A : 32'bz;  // Controlled_Buffer controlled_buffer_7
  assign RESULT = decoder_1_out8 ? A : 32'bz;  // Controlled_Buffer controlled_buffer_8
  assign RESULT = decoder_1_out9 ? multiplier_1_out : 32'bz;  // Controlled_Buffer controlled_buffer_9
  or or_3 (or_3_out, decoder_1_out3, decoder_1_out4, decoder_1_out7, decoder_1_out8, decoder_1_out9, decoder_1_out10);
  assign RESULT = decoder_1_out3 ? divider_1_out : 32'bz;  // Controlled_Buffer controlled_buffer_10
  and and_2 (and_2_out, ~decoder_1_out8, or_3_out);  // AND_Gate
  and and_3 (and_3_out, or_3_out, ~decoder_1_out7);  // AND_Gate
  Pull_Resistor pull_resistor_1 (.node(RESULT));
  Pull_Resistor pull_resistor_2 (.node(controlled_buffer_1_out));
  assign bit_extender_1_out = {{31{1'b0}}, comparator_1_lt};  // Bit_Extender bit_extender_1
  assign bit_extender_2_out = {{31{1'b0}}, comparator_2_lt};  // Bit_Extender bit_extender_2
  assign RESULT = decoder_1_out19 ? subtractor_1_out : 32'bz;  // Controlled_Buffer controlled_buffer_11
  assign RESULT = decoder_1_out20 ? xor_1_out : 32'bz;  // Controlled_Buffer controlled_buffer_12
  assign RESULT = decoder_1_out15 ? or_2_out : 32'bz;  // Controlled_Buffer controlled_buffer_13
  assign RESULT = decoder_1_out16 ? bit_extender_1_out : 32'bz;  // Controlled_Buffer controlled_buffer_14
  assign RESULT = decoder_1_out17 ? bit_extender_2_out : 32'bz;  // Controlled_Buffer controlled_buffer_15
  assign RESULT = decoder_1_out18 ? sub_1_result : 32'bz;  // Controlled_Buffer controlled_buffer_16
  assign {UNSIGNED_OVERFLOW, SIGNED_OVERFLOW} = decoder_1_out18 ? sub_1_of : 2'bz;  // Controlled_Buffer controlled_buffer_17
  assign UNSIGNED_OVERFLOW = decoder_1_out19 ? subtractor_1_bout : 1'bz;  // Controlled_Buffer controlled_buffer_18
  assign RESULT = decoder_1_out11 ? add_1_result : 32'bz;  // Controlled_Buffer controlled_buffer_19
  assign RESULT = decoder_1_out12 ? adder_1_out : 32'bz;  // Controlled_Buffer controlled_buffer_20
  assign UNSIGNED_OVERFLOW = decoder_1_out12 ? adder_1_cout : 1'bz;  // Controlled_Buffer controlled_buffer_21
  assign RESULT = decoder_1_out13 ? and_1_out : 32'bz;  // Controlled_Buffer controlled_buffer_22
  assign RESULT = decoder_1_out14 ? not_1_out : 32'bz;  // Controlled_Buffer controlled_buffer_23
  assign RESULT = decoder_1_out1 ? shifter_2_out : 32'bz;  // Controlled_Buffer controlled_buffer_24
  assign RESULT = decoder_1_out2 ? shifter_3_out : 32'bz;  // Controlled_Buffer controlled_buffer_25
  assign {UNSIGNED_OVERFLOW, SIGNED_OVERFLOW} = decoder_1_out11 ? add_1_of : 2'bz;  // Controlled_Buffer controlled_buffer_26
  Register #(.width(32)) LO (.D(RESULT), .en(and_3_out), .clk(CLK), .Q(LO_q), .clr(R));
  Pull_Resistor pull_resistor_3 (.node(RESULT));
  assign RESULT = decoder_1_out0 ? shifter_1_out : 32'bz;  // Controlled_Buffer controlled_buffer_27
  assign RESULT = decoder_1_out5 ? HI_q : 32'bz;  // Controlled_Buffer controlled_buffer_28
  assign RESULT = decoder_1_out6 ? LO_q : 32'bz;  // Controlled_Buffer controlled_buffer_29
  Pull_Resistor pull_resistor_4 (.node({UNSIGNED_OVERFLOW, SIGNED_OVERFLOW}));
  Pull_Resistor pull_resistor_5 (.node(UNSIGNED_OVERFLOW));
  Register #(.width(32)) HI (.D(controlled_buffer_1_out), .en(and_2_out), .clk(CLK), .Q(HI_q), .clr(R));

  // Notes on the sheet:
  //   I WILL NOT DO THIS CORRECTLY
endmodule
